// Logisim project ex4.circ as structural Verilog: 5 circuits, main circuit RotRight
module RotRight (
  input  [15:0] INPUT0,
  input  [3:0] AMOUNT,
  output [15:0] OUTPUT0
);

  wire [15:0] demultiplexer_1_out0, demultiplexer_1_out1, demultiplexer_2_out0, demultiplexer_2_out1,
       demultiplexer_3_out0, demultiplexer_3_out1, demultiplexer_4_out0, demultiplexer_4_out1,
       multiplexer_1_out, multiplexer_2_out, multiplexer_3_out, rot1_1_out_2, rot2_1_out_2, rot4_1_out_2,
       rot8_1_out_2;

  Demultiplexer #(.width(16)) demultiplexer_1 (
    .out0(demultiplexer_1_out0), .out1(demultiplexer_1_out1), .in(INPUT0), .sel(AMOUNT[0]));
  rot1 rot1_1 (.in_1(demultiplexer_1_out1), .out_2(rot1_1_out_2));
  Multiplexer #(.width(16)) multiplexer_1 (
    .in0(demultiplexer_1_out0), .in1(rot1_1_out_2), .out(multiplexer_1_out), .sel(AMOUNT[0]));
  Demultiplexer #(.width(16)) demultiplexer_2 (
    .out0(demultiplexer_2_out0), .out1(demultiplexer_2_out1), .in(multiplexer_1_out), .sel(AMOUNT[1]));
  Multiplexer #(.width(16)) multiplexer_2 (
    .in0(demultiplexer_2_out0), .in1(rot2_1_out_2), .out(multiplexer_2_out), .sel(AMOUNT[1]));
  rot2 rot2_1 (.in_1(demultiplexer_2_out1), .out_2(rot2_1_out_2));
  Demultiplexer #(.width(16)) demultiplexer_3 (
    .out0(demultiplexer_3_out0), .out1(demultiplexer_3_out1), .in(multiplexer_2_out), .sel(AMOUNT[2]));
  rot4 rot4_1 (.in_1(demultiplexer_3_out1), .out_2(rot4_1_out_2));
  Multiplexer #(.width(16)) multiplexer_3 (
    .in0(demultiplexer_3_out0), .in1(rot4_1_out_2), .out(multiplexer_3_out), .sel(AMOUNT[2]));
  Demultiplexer #(.width(16)) demultiplexer_4 (
    .out0(demultiplexer_4_out0), .out1(demultiplexer_4_out1), .in(multiplexer_3_out), .sel(AMOUNT[3]));
  rot8 rot8_1 (.in_1(demultiplexer_4_out1), .out_2(rot8_1_out_2));
  Multiplexer #(.width(16)) multiplexer_4 (
    .in0(demultiplexer_4_out0), .in1(rot8_1_out_2), .out(OUTPUT0), .sel(AMOUNT[3]));
endmodule

module rot1 (
  input  [15:0] in_1,
  output [15:0] out_2
);


  assign out_2 = {in_1[0], in_1[15:1]};
endmodule

module rot2 (
  input  [15:0] in_1,
  output [15:0] out_2
);


  assign out_2 = {in_1[1:0], in_1[15:2]};
endmodule

module rot4 (
  input  [15:0] in_1,
  output [15:0] out_2
);


  assign out_2 = {in_1[3:0], in_1[15:4]};
endmodule

module rot8 (
  input  [15:0] in_1,
  output [15:0] out_2
);


  assign out_2 = {in_1[7:0], in_1[15:8]};
endmodule
